// Logisim project compv4.circ as structural Verilog: 1 circuit, main circuit main
module main (
  input  in_1,
  input  clear,
  input  _2_s_COMPLIMENT,
  input  [3:0] in_4,
  input  [2:0] in_5,
  input  in_6,
  input  in_7,
  output [3:0] out_8,
  output out_9,
  output out_10,
  output out_11,
  output out_12,
  output out_13,
  output out_14,
  output out_15,
  output out_16,
  output out_17,
  output out_18,
  output out_19,
  output out_20,
  output out_21,
  output out_22,
  output out_23,
  output out_24,
  output out_25,
  output out_26,
  output out_27,
  output out_28,
  output out_29,
  output out_30,
  output out_31,
  output out_32,
  output out_33,
  output out_34,
  output out_35,
  output out_36,
  output out_37,
  output out_38,
  output out_39,
  output out_40,
  output out_41,
  output out_42,
  output out_43,
  output out_44,
  output out_45,
  output out_46,
  output out_47,
  output out_48,
  output out_49,
  output out_50,
  output out_51,
  output out_52,
  output out_53,
  output out_54
);

  wire AI, and_1_out, AO, BI, BO, CE, CF, clock_1_out, CLR, CO, decoder_1_out6, EO, FI, HLT, II, IO, JMP, MI,
       not_1_out, not_2_out, OI, or_1_out, RI, RO, SUB, ZF;
  wire [1:0] adder_1_cout;
  wire [2:0] counter_1_q, rom_1_data;
  wire [3:0] IR_LSB_q, IR_MSB_q, register_1_q;
  wire [7:0] adder_1_out, xor_1_out;
  wire [12:0] rom_2_data;

  RAM #(.addrWidth(4), .bus("separate")) ram_1 (
    .addr(register_1_q), .din({out_9, out_10, out_11, out_12, out_13, out_14, out_15, out_16}),
    .data({out_9, out_10, out_11, out_12, out_13, out_14, out_15, out_16}), .str(RI), .sel(1'b1),
    .clk(and_1_out), .ld(RO), .clr(clear));
  assign {out_13, out_14, out_15, out_16} = IO ? IR_LSB_q : 4'bz;  // Controlled_Buffer controlled_buffer_1
  Counter #(.width(3), .max('h7)) counter_1 (
    .count(not_2_out), .Q(counter_1_q), .clk(not_2_out), .clr(or_1_out));  // open: load, D, carry
  not not_1 (not_1_out, HLT);
  Clock clock_1 (.out(clock_1_out));
  and and_1 (and_1_out, not_1_out, clock_1_out);
  LED led_1 (.in(and_1_out));
  Register #(.width(4)) IR_MSB (.D({out_9, out_10, out_11, out_12}), .en(II), .Q(IR_MSB_q), .clk(and_1_out), .clr(CLR));
  Register #(.width(4)) IR_LSB (
    .D({out_13, out_14, out_15, out_16}), .en(II), .Q(IR_LSB_q), .clk(and_1_out), .clr(CLR));
  Decoder #(.select(3), .enable("false")) decoder_1 (
    .out0(out_49), .out1(out_50), .out2(out_51), .out3(out_52), .out4(out_53), .out5(out_54),
    .out6(decoder_1_out6), .sel(counter_1_q));  // open: out7
  Register #(.width(4)) register_1 (
    .D({out_13, out_14, out_15, out_16}), .en(MI), .Q(register_1_q), .clk(and_1_out), .clr(CLR));
  or or_1 (or_1_out, decoder_1_out6, CLR);
  not not_2 (not_2_out, and_1_out);
  assign {out_9, out_10, out_11, out_12, out_13, out_14, out_15, out_16} = AO ? {out_17, out_18, out_19, out_20, out_21, out_22, out_23, out_24} : 8'bz;  // Controlled_Buffer controlled_buffer_2
  assign {out_9, out_10, out_11, out_12, out_13, out_14, out_15, out_16} = BO ? {out_25, out_26, out_27, out_28, out_29, out_30, out_31, out_32} : 8'bz;  // Controlled_Buffer controlled_buffer_3
  LED led_2 (.in(HLT));
  Register register_A (
    .D({out_9, out_10, out_11, out_12, out_13, out_14, out_15, out_16}), .en(AI),
    .Q({out_17, out_18, out_19, out_20, out_21, out_22, out_23, out_24}), .clk(and_1_out), .clr(CLR));
  Register register_B (
    .D({out_9, out_10, out_11, out_12, out_13, out_14, out_15, out_16}), .en(BI),
    .Q({out_25, out_26, out_27, out_28, out_29, out_30, out_31, out_32}), .clk(and_1_out), .clr(CLR));
  Register OUT_REG (
    .D({out_9, out_10, out_11, out_12, out_13, out_14, out_15, out_16}), .en(OI),
    .Q({out_41, out_42, out_43, out_44, out_45, out_46, out_47, out_48}), .clk(and_1_out), .clr(CLR));
  LED led_3 (.in(MI));
  LED led_4 (.in(RI));
  LED led_5 (.in(RO));
  LED led_6 (.in(II));
  LED led_7 (.in(IO));
  ROM #(.addrWidth(9), .dataWidth(20)) rom_1 (
    .addr({IR_MSB_q, counter_1_q, CF, ZF}),
    .data({HLT, MI, RI, RO, IO, II, AI, AO, EO, SUB, BI, BO, OI, CE, CO, JMP, FI, rom_1_data}));  // open: sel
  Counter #(.width(4), .max('hf)) counter_2 (
    .load(JMP), .D({out_13, out_14, out_15, out_16}), .count(CE), .Q(out_8), .clk(and_1_out), .clr(CLR));  // open: carry
  LED led_8 (.in(AO));
  LED led_9 (.in(AI));
  assign {out_13, out_14, out_15, out_16} = CO ? out_8 : 4'bz;  // Controlled_Buffer controlled_buffer_4
  ROM #(.addrWidth(9), .dataWidth(13)) rom_2 (
    .addr({_2_s_COMPLIMENT, out_41, out_42, out_43, out_44, out_45, out_46, out_47, out_48}),
    .data(rom_2_data));  // open: sel
  LED led_10 (.in(SUB));
  LED led_11 (.in(EO));
  _7_Segment_Display u_7_segment_display_1 (.g(rom_2_data[12]));  // open: f, a, b, e, d, c, dp
  Hex_Digit_Display hex_digit_display_1 (.value(rom_2_data[11:8]));  // open: dp
  LED led_12 (.in(BO));
  LED led_13 (.in(BI));
  Hex_Digit_Display hex_digit_display_2 (.value(rom_2_data[7:4]));  // open: dp
  LED led_14 (.in(OI));
  assign {out_9, out_10, out_11, out_12, out_13, out_14, out_15, out_16} = EO ? adder_1_out : 8'bz;  // Controlled_Buffer controlled_buffer_5
  Hex_Digit_Display hex_digit_display_3 (.value(rom_2_data[3:0]));  // open: dp
  LED led_15 (.in(CLR));
  Button button_1 (.out(CLR));
  LED led_16 (.in(JMP));
  LED led_17 (.in(CO));
  LED led_18 (.in(CE));
  assign xor_1_out = {out_25, out_26, out_27, out_28, out_29, out_30, out_31, out_32} ^ {8{SUB}};  // XOR_Gate xor_1, 8 bits wide
  LED led_19 (.in(FI));
  Adder adder_1 (
    .a({out_17, out_18, out_19, out_20, out_21, out_22, out_23, out_24}), .b(xor_1_out), .out(adder_1_out),
    .cin(SUB), .cout(adder_1_cout[0]));
  LED led_20 (.in(adder_1_cout[0]));
  nor nor_1 (adder_1_cout[1], adder_1_out[0], adder_1_out[1], adder_1_out[2], adder_1_out[3], adder_1_out[4], adder_1_out[5], adder_1_out[6], adder_1_out[7]);
  LED led_21 (.in(adder_1_cout[1]));
  Register #(.width(2)) register_2 (.D(adder_1_cout), .en(FI), .Q({ZF, CF}), .clk(and_1_out), .clr(CLR));
  LED led_22 (.in(CF));
  LED led_23 (.in(ZF));

  assign out_33 = out_9;
  assign out_34 = out_10;
  assign out_35 = out_11;
  assign out_36 = out_12;
  assign out_37 = out_13;
  assign out_38 = out_14;
  assign out_39 = out_15;
  assign out_40 = out_16;

  // Notes on the sheet:
  //   MEM REG IN
  //   LOAD
  //   RAM
  //   EN
  //   STEP COUNTER
  //   MEMORY ADD REG.
  //   CLOCK
  //   TO ID 
  //   INSTRUCTION REG
  //   clear
  //   load
  //   ROM
  //   REG A
  //   REG B
  //   DISPLAY REG
  //   contents of rom_1 (hex, n*v repeats v):
  //   4*40020 4*14040 24*0 4*40020 4*14040 4*48000 4*12000 16*0 4*40020 4*14040 4*48000 4*10200 4*2808
  //   12*0 4*40020 4*14040 4*48000 4*10200 4*2c08 12*0 4*40020 4*14040 4*48000 4*21000 16*0 4*40020
  //   4*14040 4*a000 20*0 4*40020 4*14040 4*8010 20*0 4*40020 4*14040 0 0 8010 8010 20*0 4*40020 4*14040 0
  //   8010 0 8010 20*0 4*40020 4*14040 4*1200 20*0 4*40020 4*14040 4*2100 20*0 4*40020 4*14040 24*0
  //   4*40020 4*14040 24*0 4*40020 4*14040 24*0 4*40020 4*14040 4*1080 20*0 4*40020 4*14040 4*80000
  //   PROGRAM COUNTER
  //   load
  //   enable
  //   clear
  //   load
  //   enable
  //   clear
  //   contents of rom_2 (hex, n*v repeats v):
  //   0 1 2 3 4 5 6 7 8 9 10 11 12 13 14 15 16 17 18 19 20 21 22 23 24 25 26 27 28 29 30 31 32 33 34 35 36
  //   37 38 39 40 41 42 43 44 45 46 47 48 49 50 51 52 53 54 55 56 57 58 59 60 61 62 63 64 65 66 67 68 69
  //   70 71 72 73 74 75 76 77 78 79 80 81 82 83 84 85 86 87 88 89 90 91 92 93 94 95 96 97 98 99 100 101
  //   102 103 104 105 106 107 108 109 110 111 112 113 114 115 116 117 118 119 120 121 122 123 124 125 126
  //   127 128 129 130 131 132 133 134 135 136 137 138 139 140 141 142 143 144 145 146 147 148 149 150 151
  //   152 153 154 155 156 157 158 159 160 161 162 163 164 165 166 167 168 169 170 171 172 173 174 175 176
  //   177 178 179 180 181 182 183 184 185 186 187 188 189 190 191 192 193 194 195 196 197 198 199 200 201
  //   202 203 204 205 206 207 208 209 210 211 212 213 214 215 216 217 218 219 220 221 222 223 224 225 226
  //   227 228 229 230 231 232 233 234 235 236 237 238 239 240 241 242 243 244 245 246 247 248 249 250 251
  //   252 253 254 255 0 1 2 3 4 5 6 7 8 9 10 11 12 13 14 15 16 17 18 19 20 21 22 23 24 25 26 27 28 29 30
  //   31 32 33 34 35 36 37 38 39 40 41 42 43 44 45 46 47 48 49 50 51 52 53 54 55 56 57 58 59 60 61 62 63
  //   64 65 66 67 68 69 70 71 72 73 74 75 76 77 78 79 80 81 82 83 84 85 86 87 88 89 90 91 92 93 94 95 96
  //   97 98 99 100 101 102 103 104 105 106 107 108 109 110 111 112 113 114 115 116 117 118 119 120 121 122
  //   123 124 125 126 127 1128 1127 1126 1125 1124 1123 1122 1121 1120 1119 1118 1117 1116 1115 1114 1113
  //   1112 1111 1110 1109 1108 1107 1106 1105 1104 1103 1102 1101 1100 1099 1098 1097 1096 1095 1094 1093
  //   1092 1091 1090 1089 1088 1087 1086 1085 1084 1083 1082 1081 1080 1079 1078 1077 1076 1075 1074 1073
  //   1072 1071 1070 1069 1068 1067 1066 1065 1064 1063 1062 1061 1060 1059 1058 1057 1056 1055 1054 1053
  //   1052 1051 1050 1049 1048 1047 1046 1045 1044 1043 1042 1041 1040 1039 1038 1037 1036 1035 1034 1033
  //   1032 1031 1030 1029 1028 1027 1026 1025 1024 1023 1022 1021 1020 1019 1018 1017 1016 1015 1014 1013
  //   1012 1011 1010 1009 1008 1007 1006 1005 1004 1003 1002 1001
  //   RESET
  //   ALU
  //   carry flag
  //   zero flag
  //   FLAG REGISTER
endmodule
